// Logisim project RV32_IM.circ as structural Verilog: 4 circuits, main circuit main
module main (
);

  wire CLK, RAM_WRITE_EN;
  wire [31:0] RAM_ADDR, RAM_READ_DATA, RAM_WRITE_DATA, ROM_ADDR, ROM_DATA;

  CPU cpu_1 (
    .Outputs(RAM_ADDR), .out_5(RAM_WRITE_DATA), .out_6(RAM_WRITE_EN), .out_7(ROM_ADDR),
    .Inputs(RAM_READ_DATA), .in_2(ROM_DATA), .in_3(CLK));
  RAM #(.addrWidth(10), .dataWidth(32), .enables("line")) ram_1 (
    .addr(RAM_ADDR[9:0]), .we(RAM_WRITE_EN), .clk(CLK), .din(RAM_WRITE_DATA), .dout(RAM_READ_DATA));
  Clock clock_1 (.out(CLK));
  ROM #(.addrWidth(10), .dataWidth(32)) rom_1 (.addr(ROM_ADDR[9:0]), .data(ROM_DATA));

  // Notes on the sheet:
  //   CPU
  //   RAM
  //   RISC-V Bilgisayar (RV32IM)
  //   Emin FEDAR | 2020
  //   ROM
  //   contents of rom_1 (hex, n*v repeats v):
  //   0 100313 100593 a00613 b32023 32583 158593 b32023 fec5cae3 13
endmodule

module CPU (
  input  [31:0] Inputs,
  input  [31:0] in_2,
  input  in_3,
  output [31:0] Outputs,
  output [31:0] out_5,
  output out_6,
  output [31:0] out_7
);

  wire and_1_out, and_2_out, and_3_out, and_4_out, B_beq, B_blt, B_bltu, B_TYPE, comparator_11_eq,
       comparator_11_gt, comparator_12_eq, comparator_13_eq, comparator_14_eq, comparator_15_eq,
       comparator_16_eq, comparator_17_eq, comparator_18_eq, comparator_19_eq, comparator_20_eq,
       comparator_21_eq, comparator_22_eq, comparator_23_eq, comparator_24_eq, comparator_25_eq,
       comparator_26_eq, comparator_27_eq, comparator_28_eq, comparator_29_eq, comparator_30_eq,
       comparator_31_eq, comparator_32_eq, comparator_33_eq, comparator_34_eq, comparator_35_eq,
       comparator_36_eq, comparator_37_eq, comparator_38_eq, comparator_39_eq, comparator_40_eq,
       comparator_41_eq, comparator_42_eq, comparator_43_eq, comparator_44_eq, comparator_45_eq,
       comparator_46_eq, comparator_47_eq, comparator_48_eq, comparator_49_eq, comparator_50_eq,
       comparator_51_eq, comparator_52_eq, comparator_53_eq, comparator_54_eq, comparator_55_eq,
       comparator_56_eq, comparator_57_eq, I_add, I_and, I_jalr, I_lb, I_lh, I_lw, I_or, I_sll, I_slt, I_srl,
       I_TYPE, I_TYPE_LOAD, I_TYPE_OTHER, I_xor, isEqual, largeOrEqual, lessSigned, lessUnsigned, or_1_out,
       or_2_out, or_3_out, or_4_out, or_5_out, or_6_out, or_7_out, or_8_out, or_9_out, or_10_out, or_12_out,
       or_13_out, PC_ALU_SEL, R_add, R_and, R_div, R_mul, R_mulh, R_or, R_rem, R_sll, R_slt, R_srl, R_sub,
       R_TYPE, R_xor, Reg_WE, S_sw, S_swge, S_TYPE, U_jal, U_lui, U_TYPE;
  wire [1:0] ALU_X1_Sel, ALU_X2_Sel, WB_Sel;
  wire [2:0] Imm_Sel;
  wire [3:0] ALU_OP;
  wire [31:0] ALU_OUT, ALU_X1, ALU_X2, Imm_B, Imm_I, Imm_S, Imm_UJ, Imm_Value, multiplexer_3_out, PC_1, PCx4,
       R1_DATA, shifter_1_out, WRITE_BACK_DATA;

  or or_1 (or_1_out, R_add, I_add);
  or or_2 (or_2_out, R_and, I_and);
  or or_3 (or_3_out, R_or, I_or);
  or or_4 (or_4_out, R_xor, I_xor);
  or or_5 (or_5_out, R_sll, I_sll);
  or or_6 (or_6_out, R_srl, I_srl);
  or or_7 (or_7_out, R_slt, I_slt);
  Shifter #(.shift("lr"), .width(32)) shifter_1 (.in(ALU_OUT), .\dist (5'b00010), .out(shifter_1_out));
  REGISTERS registers_1 (
    .Outputs(R1_DATA), .out_8(out_5), .in_5(Reg_WE), .in_6(in_3), .in_1(in_2[19:15]), .in_2(in_2[24:20]),
    .in_3(in_2[11:7]), .in_4(WRITE_BACK_DATA));
  Multiplexer #(.enable("false"), .select(2), .width(32)) multiplexer_1 (
    .in0(R1_DATA), .in1(PCx4), .in2({32{1'b0}}), .out(ALU_X1), .sel(ALU_X1_Sel));  // open: in3
  Multiplexer #(.enable("false"), .select(2), .width(32)) multiplexer_2 (
    .in0(out_5), .in1(Imm_Value), .in2({32{1'b0}}), .out(ALU_X2), .sel(ALU_X2_Sel));  // open: in3
  or or_8 (or_8_out, B_TYPE, U_jal);
  or or_9 (or_9_out, S_sw, I_TYPE, B_TYPE, U_TYPE);
  Multiplexer #(.enable("false"), .width(32)) multiplexer_3 (
    .in0(PC_1), .in1(shifter_1_out), .out(multiplexer_3_out), .sel(PC_ALU_SEL));
  Priority_Encoder #(.select(4)) priority_encoder_1 (
    .in0(or_1_out), .in1(R_sub), .in2(or_2_out), .in3(or_3_out), .in4(or_4_out), .in5(or_5_out),
    .in6(or_6_out), .in7(R_mul), .in8(R_mulh), .in9(R_div), .in10(R_rem), .in11(or_7_out), .out(ALU_OP));  // open: in12, in13, in14, in15, gs, en_out, en_in
  Priority_Encoder #(.select(2)) priority_encoder_2 (
    .in0(1'b1), .in1(or_8_out), .in2(U_lui), .out(ALU_X1_Sel));  // open: in3, gs, en_out, en_in
  Priority_Encoder #(.select(2)) priority_encoder_3 (
    .in0(1'b1), .in1(or_9_out), .in2(S_swge), .out(ALU_X2_Sel));  // open: in3, gs, en_out, en_in
  Adder #(.width(32)) adder_1 (.a(out_7), .b(32'h1), .out(PC_1));  // open: cin, cout
  Shifter #(.width(32)) shifter_2 (.in(out_7), .\dist (5'b00010), .out(PCx4));
  Register #(.width(32)) register_1 (.D(multiplexer_3_out), .en(in_3), .clk(in_3), .Q(out_7));  // open: clr
  ALU alu_1 (.Outputs(ALU_OUT), .out_5(isEqual), .in_1(ALU_X1), .in_2(ALU_X2), .in_3(ALU_OP));
  assign Imm_I = {{20{in_2[31]}}, in_2[31:20]};  // Bit_Extender bit_extender_1
  assign Imm_S = {{20{in_2[31]}}, {in_2[31:25], in_2[11:7]}};  // Bit_Extender bit_extender_2
  Priority_Encoder priority_encoder_4 (
    .in0(I_TYPE), .in1(U_lui), .in2(S_TYPE), .in3(B_TYPE), .in4(U_jal), .out(Imm_Sel));  // open: in5, in6, in7, en_in, gs, en_out
  and and_1 (and_1_out, B_beq, isEqual);
  and and_2 (and_2_out, B_blt, lessSigned);
  and and_3 (and_3_out, B_bltu, lessUnsigned);
  or or_10 (or_10_out, I_jalr, U_jal);
  Comparator #(.width(32)) comparator_1 (.a(R1_DATA), .b(out_5), .lt(lessSigned));  // open: gt, eq
  Comparator #(.width(32)) comparator_2 (.a(R1_DATA), .b(out_5), .lt(lessUnsigned));  // open: gt, eq
  or or_11 (PC_ALU_SEL, and_1_out, and_2_out, and_3_out, or_10_out);
  assign Imm_B = {{19{in_2[31]}}, {in_2[31], in_2[7], in_2[30:25], in_2[11:8], 1'b0}};  // Bit_Extender bit_extender_3
  assign Imm_UJ = {{11{in_2[31]}}, {in_2[31], in_2[19:12], in_2[20], in_2[30:21], 1'b0}};  // Bit_Extender bit_extender_4
  Multiplexer #(.enable("false"), .select(3), .width(32)) multiplexer_4 (
    .in0(Imm_I), .in1({in_2[31:12], {12{1'b0}}}), .in2(Imm_S), .in3(Imm_B), .in4(Imm_UJ), .out(Imm_Value),
    .sel(Imm_Sel));  // open: in5, in6, in7
  or or_12 (or_12_out, R_TYPE, U_lui, I_TYPE_OTHER);
  or or_13 (or_13_out, U_jal, I_jalr);
  and and_4 (and_4_out, S_swge, largeOrEqual);
  Comparator #(.width(7)) comparator_3 (.a(in_2[6:0]), .b(7'b0110011), .eq(R_TYPE));  // open: gt, lt
  Comparator #(.width(7)) comparator_4 (.a(in_2[6:0]), .b(7'b0000011), .eq(I_TYPE_LOAD));  // open: gt, lt
  Comparator #(.width(7)) comparator_5 (.a(in_2[6:0]), .b(7'b0010011), .eq(I_TYPE_OTHER));  // open: gt, lt
  Comparator #(.width(7)) comparator_6 (.a(in_2[6:0]), .b(7'b0100011), .eq(S_TYPE));  // open: gt, lt
  Comparator #(.width(7)) comparator_7 (.a(in_2[6:0]), .b(7'b1100011), .eq(B_TYPE));  // open: gt, lt
  Comparator #(.width(7)) comparator_8 (.a(in_2[6:0]), .b(7'b0110111), .eq(U_lui));  // open: gt, lt
  Comparator #(.width(7)) comparator_9 (.a(in_2[6:0]), .b(7'b1100111), .eq(U_jal));  // open: gt, lt
  Comparator #(.width(7)) comparator_10 (.a(in_2[6:0]), .b(7'b1101111), .eq(I_jalr));  // open: gt, lt
  or or_14 (U_TYPE, U_lui, U_jal);
  or or_15 (I_TYPE, I_TYPE_LOAD, I_TYPE_OTHER, I_jalr);
  or or_16 (Reg_WE, R_TYPE, I_TYPE, U_TYPE);
  Multiplexer #(.enable("false"), .select(2), .width(32)) multiplexer_5 (
    .in0(Inputs), .in1(ALU_OUT), .in2(PC_1), .out(WRITE_BACK_DATA), .sel(WB_Sel));  // open: in3
  or or_17 (out_6, S_sw, and_4_out);
  or or_18 (largeOrEqual, comparator_11_gt, comparator_11_eq);
  Comparator #(.width(32)) comparator_11 (
    .a(R1_DATA), .b(Imm_Value), .gt(comparator_11_gt), .eq(comparator_11_eq));  // open: lt
  Adder #(.width(32)) adder_2 (.a(Imm_Value), .b(R1_DATA), .out(Outputs));  // open: cin, cout
  Priority_Encoder #(.select(2)) priority_encoder_5 (
    .in0(I_TYPE_LOAD), .in1(or_12_out), .in2(or_13_out), .out(WB_Sel));  // open: in3, gs, en_out, en_in
  Comparator #(.width(3)) comparator_12 (.a(in_2[14:12]), .b(3'b000), .eq(comparator_12_eq));  // open: gt, lt
  Comparator #(.width(7)) comparator_13 (.a(in_2[31:25]), .b({7{1'b0}}), .eq(comparator_13_eq));  // open: gt, lt
  Comparator #(.width(3)) comparator_14 (.a(in_2[14:12]), .b(3'b000), .eq(comparator_14_eq));  // open: gt, lt
  Comparator #(.width(7)) comparator_15 (.a(in_2[31:25]), .b(7'b0000001), .eq(comparator_15_eq));  // open: gt, lt
  Comparator #(.width(3)) comparator_16 (.a(in_2[14:12]), .b(3'b000), .eq(comparator_16_eq));  // open: gt, lt
  Comparator #(.width(7)) comparator_17 (.a(in_2[31:25]), .b(7'b0100000), .eq(comparator_17_eq));  // open: gt, lt
  Comparator #(.width(3)) comparator_18 (.a(in_2[14:12]), .b(3'b001), .eq(comparator_18_eq));  // open: gt, lt
  Comparator #(.width(7)) comparator_19 (.a(in_2[31:25]), .b({7{1'b0}}), .eq(comparator_19_eq));  // open: gt, lt
  Comparator #(.width(3)) comparator_20 (.a(in_2[14:12]), .b(3'b001), .eq(comparator_20_eq));  // open: gt, lt
  Comparator #(.width(7)) comparator_21 (.a(in_2[31:25]), .b(7'b0000001), .eq(comparator_21_eq));  // open: gt, lt
  Comparator #(.width(3)) comparator_22 (.a(in_2[14:12]), .b(3'b010), .eq(comparator_22_eq));  // open: gt, lt
  Comparator #(.width(7)) comparator_23 (.a(in_2[31:25]), .b({7{1'b0}}), .eq(comparator_23_eq));  // open: gt, lt
  and and_5 (R_add, R_TYPE, comparator_12_eq, comparator_13_eq);
  and and_6 (R_mul, R_TYPE, comparator_14_eq, comparator_15_eq);
  and and_7 (R_sub, R_TYPE, comparator_16_eq, comparator_17_eq);
  and and_8 (R_sll, R_TYPE, comparator_18_eq, comparator_19_eq);
  and and_9 (R_mulh, R_TYPE, comparator_20_eq, comparator_21_eq);
  and and_10 (R_slt, R_TYPE, comparator_22_eq, comparator_23_eq);
  Comparator #(.width(3)) comparator_24 (.a(in_2[14:12]), .b(3'b100), .eq(comparator_24_eq));  // open: gt, lt
  Comparator #(.width(7)) comparator_25 (.a(in_2[31:25]), .b({7{1'b0}}), .eq(comparator_25_eq));  // open: gt, lt
  Comparator #(.width(3)) comparator_26 (.a(in_2[14:12]), .b(3'b100), .eq(comparator_26_eq));  // open: gt, lt
  Comparator #(.width(7)) comparator_27 (.a(in_2[31:25]), .b(7'b0000001), .eq(comparator_27_eq));  // open: gt, lt
  Comparator #(.width(3)) comparator_28 (.a(in_2[14:12]), .b(3'b101), .eq(comparator_28_eq));  // open: gt, lt
  Comparator #(.width(7)) comparator_29 (.a(in_2[31:25]), .b({7{1'b0}}), .eq(comparator_29_eq));  // open: gt, lt
  Comparator #(.width(3)) comparator_30 (.a(in_2[14:12]), .b(3'b110), .eq(comparator_30_eq));  // open: gt, lt
  Comparator #(.width(7)) comparator_31 (.a(in_2[31:25]), .b({7{1'b0}}), .eq(comparator_31_eq));  // open: gt, lt
  Comparator #(.width(3)) comparator_32 (.a(in_2[14:12]), .b(3'b110), .eq(comparator_32_eq));  // open: gt, lt
  Comparator #(.width(7)) comparator_33 (.a(in_2[31:25]), .b(7'b0000001), .eq(comparator_33_eq));  // open: gt, lt
  Comparator #(.width(3)) comparator_34 (.a(in_2[14:12]), .b(3'b111), .eq(comparator_34_eq));  // open: gt, lt
  Comparator #(.width(7)) comparator_35 (.a(in_2[31:25]), .b({7{1'b0}}), .eq(comparator_35_eq));  // open: gt, lt
  and and_11 (R_xor, R_TYPE, comparator_24_eq, comparator_25_eq);
  and and_12 (R_div, R_TYPE, comparator_26_eq, comparator_27_eq);
  and and_13 (R_srl, R_TYPE, comparator_28_eq, comparator_29_eq);
  and and_14 (R_or, R_TYPE, comparator_30_eq, comparator_31_eq);
  and and_15 (R_rem, R_TYPE, comparator_32_eq, comparator_33_eq);
  and and_16 (R_and, R_TYPE, comparator_34_eq, comparator_35_eq);
  Comparator #(.width(3)) comparator_36 (.a(in_2[14:12]), .b(3'b000), .eq(comparator_36_eq));  // open: gt, lt
  Comparator #(.width(3)) comparator_37 (.a(in_2[14:12]), .b(3'b001), .eq(comparator_37_eq));  // open: gt, lt
  Comparator #(.width(3)) comparator_38 (.a(in_2[14:12]), .b(3'b010), .eq(comparator_38_eq));  // open: gt, lt
  and and_17 (I_lb, I_TYPE_LOAD, comparator_36_eq);
  and and_18 (I_lh, I_TYPE_LOAD, comparator_37_eq);
  and and_19 (I_lw, I_TYPE_LOAD, comparator_38_eq);
  Comparator #(.width(3)) comparator_39 (.a(in_2[14:12]), .b(3'b000), .eq(comparator_39_eq));  // open: gt, lt
  Comparator #(.width(7)) comparator_40 (.a(in_2[31:25]), .b({7{1'b0}}), .eq(comparator_40_eq));  // open: gt, lt
  Comparator #(.width(3)) comparator_41 (.a(in_2[14:12]), .b(3'b001), .eq(comparator_41_eq));  // open: gt, lt
  Comparator #(.width(7)) comparator_42 (.a(in_2[31:25]), .b({7{1'b0}}), .eq(comparator_42_eq));  // open: gt, lt
  Comparator #(.width(3)) comparator_43 (.a(in_2[14:12]), .b(3'b010), .eq(comparator_43_eq));  // open: gt, lt
  Comparator #(.width(7)) comparator_44 (.a(in_2[31:25]), .b({7{1'b0}}), .eq(comparator_44_eq));  // open: gt, lt
  Comparator #(.width(3)) comparator_45 (.a(in_2[14:12]), .b(3'b100), .eq(comparator_45_eq));  // open: gt, lt
  Comparator #(.width(7)) comparator_46 (.a(in_2[31:25]), .b({7{1'b0}}), .eq(comparator_46_eq));  // open: gt, lt
  Comparator #(.width(3)) comparator_47 (.a(in_2[14:12]), .b(3'b101), .eq(comparator_47_eq));  // open: gt, lt
  Comparator #(.width(7)) comparator_48 (.a(in_2[31:25]), .b({7{1'b0}}), .eq(comparator_48_eq));  // open: gt, lt
  and and_20 (I_add, I_TYPE_OTHER, comparator_39_eq, comparator_40_eq);
  and and_21 (I_sll, I_TYPE_OTHER, comparator_41_eq, comparator_42_eq);
  and and_22 (I_slt, I_TYPE_OTHER, comparator_43_eq, comparator_44_eq);
  and and_23 (I_xor, I_TYPE_OTHER, comparator_45_eq, comparator_46_eq);
  and and_24 (I_srl, I_TYPE_OTHER, comparator_47_eq, comparator_48_eq);
  Comparator #(.width(3)) comparator_49 (.a(in_2[14:12]), .b(3'b110), .eq(comparator_49_eq));  // open: gt, lt
  Comparator #(.width(7)) comparator_50 (.a(in_2[31:25]), .b({7{1'b0}}), .eq(comparator_50_eq));  // open: gt, lt
  Comparator #(.width(3)) comparator_51 (.a(in_2[14:12]), .b(3'b111), .eq(comparator_51_eq));  // open: gt, lt
  Comparator #(.width(7)) comparator_52 (.a(in_2[31:25]), .b({7{1'b0}}), .eq(comparator_52_eq));  // open: gt, lt
  and and_25 (I_or, I_TYPE_OTHER, comparator_49_eq, comparator_50_eq);
  and and_26 (I_and, I_TYPE_OTHER, comparator_51_eq, comparator_52_eq);
  Comparator #(.width(3)) comparator_53 (.a(in_2[14:12]), .b(3'b010), .eq(comparator_53_eq));  // open: gt, lt
  Comparator #(.width(3)) comparator_54 (.a(in_2[14:12]), .b(3'b111), .eq(comparator_54_eq));  // open: gt, lt
  and and_27 (S_sw, S_TYPE, comparator_53_eq);
  and and_28 (S_swge, S_TYPE, comparator_54_eq);
  Comparator #(.width(3)) comparator_55 (.a(in_2[14:12]), .b(3'b000), .eq(comparator_55_eq));  // open: gt, lt
  Comparator #(.width(3)) comparator_56 (.a(in_2[14:12]), .b(3'b100), .eq(comparator_56_eq));  // open: gt, lt
  Comparator #(.width(3)) comparator_57 (.a(in_2[14:12]), .b(3'b110), .eq(comparator_57_eq));  // open: gt, lt
  and and_29 (B_beq, B_TYPE, comparator_55_eq);
  and and_30 (B_blt, B_TYPE, comparator_56_eq);
  and and_31 (B_bltu, B_TYPE, comparator_57_eq);

  // Other names for the same wires on the sheet: IMM_4_0[4:0] = in_2[11:7]; IMM_4_1[3:0] = in_2[11:8];
  //   INSTRUCTION[31:0] = in_2; RD[4:0] = in_2[11:7]; IMM_11_B = in_2[7]; IMM_10_1[9:0] = in_2[30:21];
  //   IMM_11_0[11:0] = in_2[31:20]; IMM_31_12[19:0] = in_2[31:12]; Imm_U[31:12] = in_2[31:12]; R2[4:0] = in_2[24:20];
  //   FUNCT7[6:0] = in_2[31:25]; IMM_10_5[5:0] = in_2[30:25]; IMM_11_5[6:0] = in_2[31:25]; IMM_11_J = in_2[20];
  //   FUNCT3[2:0] = in_2[14:12]; IMM_19_12[7:0] = in_2[19:12]; R1[4:0] = in_2[19:15]; IMM_12 = in_2[31];
  //   IMM_20 = in_2[31]; CLK = in_3; I_TYPE_JUMP = I_jalr; OPCODE[6:0] = in_2[6:0]; INSTRUCTION_ADDR[31:0] = out_7;
  //   PC[31:0] = out_7; RAM_ADDR[31:0] = Outputs; RAM_READ_DATA[31:0] = Inputs; R2_DATA[31:0] = out_5;
  //   RAM_WRITE_DATA[31:0] = out_5; RAM_WRITE_EN = out_6; U_TYPE_JUMP = U_jal; U_TYPE_LOAD = U_lui

  // Notes on the sheet:
  //   I/O
  //   1.FETCH
  //   3. REGISTERS
  //   4. EXECUTE
  //   ALU Operation Encoding
  //   ALU Inputs
  //   ALU Input Selections
  //   ALU
  //   Immediate Value Selection
  //   PC MUX Selection
  //   2.DECODE
  //   I-Type
  //   U-Type
  //   S-Type
  //   INSTRUCTION Parameterization
  //   R-Type
  //   I-Type
  //   U-Type
  //   S-Type
  //   B-Type
  //   J-Type
  //   B-Type
  //   UJ-Type
  //   5. WRITE BACK
  //   Register Write Enable
  //   Register Write Back
  //   6. MEMORY WRITE
  //   Memory Write Selection
  //   Memory Write Data/Addr
  //   INSTRUCTION DECODING
endmodule

module REGISTERS (
  input  [4:0] in_1,
  input  [4:0] in_2,
  input  [4:0] in_3,
  input  [31:0] in_4,
  input  in_5,
  input  in_6,
  output [31:0] Outputs,
  output [31:0] out_8
);

  wire WE_1, WE_2, WE_3, WE_4, WE_5, WE_6, WE_7, WE_8, WE_9, WE_10, WE_11, WE_12, WE_13, WE_14, WE_15, WE_16,
       WE_17, WE_18, WE_19, WE_20, WE_21, WE_22, WE_23, WE_24, WE_25, WE_26, WE_27, WE_28, WE_29, WE_30,
       WE_31;
  wire [31:0] in_r1, in_r2, in_r3, in_r4, in_r5, in_r6, in_r7, in_r8, in_r9, in_r10, in_r11, in_r12, in_r13,
       in_r14, in_r15, in_r16, in_r17, in_r18, in_r19, in_r20, in_r21, in_r22, in_r23, in_r24, in_r25,
       in_r26, in_r27, in_r28, in_r29, in_r30, in_r31, out_r1, out_r2, out_r3, out_r4, out_r5, out_r6,
       out_r7, out_r8, out_r9, out_r10, out_r11, out_r12, out_r13, out_r14, out_r15, out_r16, out_r17,
       out_r18, out_r19, out_r20, out_r21, out_r22, out_r23, out_r24, out_r25, out_r26, out_r27, out_r28,
       out_r29, out_r30, out_r31;

  Register #(.width(32)) r1 (.D(in_r1), .en(WE_1), .clk(in_6), .Q(out_r1));  // open: clr
  Register #(.width(32)) register_1 (.D(in_r9), .en(WE_9), .clk(in_6), .Q(out_r9));  // open: clr
  Register #(.width(32)) register_2 (.D(in_r17), .en(WE_17), .clk(in_6), .Q(out_r17));  // open: clr
  Register #(.width(32)) register_3 (.D(in_r25), .en(WE_25), .clk(in_6), .Q(out_r25));  // open: clr
  Multiplexer #(.enable("false"), .select(5), .width(32)) multiplexer_1 (
    .in0({32{1'b0}}), .in1(out_r1), .in2(out_r2), .in3(out_r3), .in4(out_r4), .in5(out_r5), .in6(out_r6),
    .in7(out_r7), .in8(out_r8), .in9(out_r9), .in10(out_r10), .in11(out_r11), .in12(out_r12), .in13(out_r13),
    .in14(out_r14), .in15(out_r15), .in16(out_r16), .in17(out_r17), .in18(out_r18), .in19(out_r19),
    .in20(out_r20), .in21(out_r21), .in22(out_r22), .in23(out_r23), .in24(out_r24), .in25(out_r25),
    .in26(out_r26), .in27(out_r27), .in28(out_r28), .in29(out_r29), .in30(out_r30), .in31(out_r31),
    .out(Outputs), .sel(in_1));
  Register #(.width(32)) register_4 (.D(in_r2), .en(WE_2), .clk(in_6), .Q(out_r2));  // open: clr
  Register #(.width(32)) register_5 (.D(in_r10), .en(WE_10), .clk(in_6), .Q(out_r10));  // open: clr
  Register #(.width(32)) register_6 (.D(in_r18), .en(WE_18), .clk(in_6), .Q(out_r18));  // open: clr
  Register #(.width(32)) register_7 (.D(in_r26), .en(WE_26), .clk(in_6), .Q(out_r26));  // open: clr
  Register #(.width(32)) register_8 (.D(in_r3), .en(WE_3), .clk(in_6), .Q(out_r3));  // open: clr
  Register #(.width(32)) register_9 (.D(in_r11), .en(WE_11), .clk(in_6), .Q(out_r11));  // open: clr
  Register #(.width(32)) register_10 (.D(in_r19), .en(WE_19), .clk(in_6), .Q(out_r19));  // open: clr
  Register #(.width(32)) register_11 (.D(in_r27), .en(WE_27), .clk(in_6), .Q(out_r27));  // open: clr
  Multiplexer #(.enable("false"), .select(5), .width(32)) multiplexer_2 (
    .in0({32{1'b0}}), .in1(out_r1), .in2(out_r2), .in3(out_r3), .in4(out_r4), .in5(out_r5), .in6(out_r6),
    .in7(out_r7), .in8(out_r8), .in9(out_r9), .in10(out_r10), .in11(out_r11), .in12(out_r12), .in13(out_r13),
    .in14(out_r14), .in15(out_r15), .in16(out_r16), .in17(out_r17), .in18(out_r18), .in19(out_r19),
    .in20(out_r20), .in21(out_r21), .in22(out_r22), .in23(out_r23), .in24(out_r24), .in25(out_r25),
    .in26(out_r26), .in27(out_r27), .in28(out_r28), .in29(out_r29), .in30(out_r30), .in31(out_r31),
    .out(out_8), .sel(in_2));
  Register #(.width(32)) register_12 (.D(in_r4), .en(WE_4), .clk(in_6), .Q(out_r4));  // open: clr
  Register #(.width(32)) register_13 (.D(in_r12), .en(WE_12), .clk(in_6), .Q(out_r12));  // open: clr
  Register #(.width(32)) register_14 (.D(in_r20), .en(WE_20), .clk(in_6), .Q(out_r20));  // open: clr
  Register #(.width(32)) register_15 (.D(in_r28), .en(WE_28), .clk(in_6), .Q(out_r28));  // open: clr
  Demultiplexer #(.select(5), .width(32)) demultiplexer_1 (
    .out1(in_r1), .out2(in_r2), .out3(in_r3), .out4(in_r4), .out5(in_r5), .out6(in_r6), .out7(in_r7),
    .out8(in_r8), .out9(in_r9), .out10(in_r10), .out11(in_r11), .out12(in_r12), .out13(in_r13),
    .out14(in_r14), .out15(in_r15), .out16(in_r16), .out17(in_r17), .out18(in_r18), .out19(in_r19),
    .out20(in_r20), .out21(in_r21), .out22(in_r22), .out23(in_r23), .out24(in_r24), .out25(in_r25),
    .out26(in_r26), .out27(in_r27), .out28(in_r28), .out29(in_r29), .out30(in_r30), .out31(in_r31),
    .in(in_4), .sel(in_3), .en(in_5));  // open: out0
  Register #(.width(32)) register_16 (.D(in_r5), .en(WE_5), .clk(in_6), .Q(out_r5));  // open: clr
  Register #(.width(32)) register_17 (.D(in_r13), .en(WE_13), .clk(in_6), .Q(out_r13));  // open: clr
  Register #(.width(32)) register_18 (.D(in_r21), .en(WE_21), .clk(in_6), .Q(out_r21));  // open: clr
  Register #(.width(32)) register_19 (.D(in_r29), .en(WE_29), .clk(in_6), .Q(out_r29));  // open: clr
  Register #(.width(32)) register_20 (.D(in_r6), .en(WE_6), .clk(in_6), .Q(out_r6));  // open: clr
  Register #(.width(32)) register_21 (.D(in_r14), .en(WE_14), .clk(in_6), .Q(out_r14));  // open: clr
  Register #(.width(32)) register_22 (.D(in_r22), .en(WE_22), .clk(in_6), .Q(out_r22));  // open: clr
  Register #(.width(32)) register_23 (.D(in_r30), .en(WE_30), .clk(in_6), .Q(out_r30));  // open: clr
  Decoder #(.select(5)) decoder_1 (
    .out1(WE_1), .out2(WE_2), .out3(WE_3), .out4(WE_4), .out5(WE_5), .out6(WE_6), .out7(WE_7), .out8(WE_8),
    .out9(WE_9), .out10(WE_10), .out11(WE_11), .out12(WE_12), .out13(WE_13), .out14(WE_14), .out15(WE_15),
    .out16(WE_16), .out17(WE_17), .out18(WE_18), .out19(WE_19), .out20(WE_20), .out21(WE_21), .out22(WE_22),
    .out23(WE_23), .out24(WE_24), .out25(WE_25), .out26(WE_26), .out27(WE_27), .out28(WE_28), .out29(WE_29),
    .out30(WE_30), .out31(WE_31), .sel(in_3), .en(in_5));  // open: out0
  Register #(.width(32)) register_24 (.D(in_r7), .en(WE_7), .clk(in_6), .Q(out_r7));  // open: clr
  Register #(.width(32)) register_25 (.D(in_r15), .en(WE_15), .clk(in_6), .Q(out_r15));  // open: clr
  Register #(.width(32)) register_26 (.D(in_r23), .en(WE_23), .clk(in_6), .Q(out_r23));  // open: clr
  Register #(.width(32)) register_27 (.D(in_r31), .en(WE_31), .clk(in_6), .Q(out_r31));  // open: clr
  Register #(.width(32)) register_28 (.D(in_r8), .en(WE_8), .clk(in_6), .Q(out_r8));  // open: clr
  Register #(.width(32)) register_29 (.D(in_r16), .en(WE_16), .clk(in_6), .Q(out_r16));  // open: clr
  Register #(.width(32)) register_30 (.D(in_r24), .en(WE_24), .clk(in_6), .Q(out_r24));  // open: clr

  // Other names for the same wires on the sheet: CLK = in_6; reg1[4:0] = in_1; reg1_data[31:0] = Outputs;
  //   reg2[4:0] = in_2; reg2_data[31:0] = out_8; reg_write[4:0] = in_3; reg_write_data[31:0] = in_4; WE = in_5

  // Notes on the sheet:
  //   I/O
  //   Inputs
  //   Register Reading
  //   Register Writing
endmodule

module ALU (
  input  [31:0] in_1,
  input  [31:0] in_2,
  input  [3:0] in_3,
  output [31:0] Outputs,
  output out_5
);

  wire comparator_1_lt;
  wire [31:0] o_add, o_and, o_div, o_mul, o_mulh, o_or, o_rem, o_sll, o_slt, o_srl, o_sub, o_xor;

  Multiplexer #(.enable("false"), .select(4), .width(32)) multiplexer_1 (
    .in0(o_add), .in1(o_sub), .in2(o_and), .in3(o_or), .in4(o_xor), .in5(o_sll), .in6(o_srl), .in7(o_mul),
    .in8(o_mulh), .in9(o_div), .in10(o_rem), .in11(o_slt), .out(Outputs), .sel(in_3));  // open: in12, in13, in14, in15
  Adder #(.width(32)) adder_1 (.a(in_1), .b(in_2), .out(o_add));  // open: cin, cout
  Subtractor #(.width(32)) subtractor_1 (.a(in_1), .b(in_2), .out(o_sub));  // open: bin, bout
  assign o_and = in_1 & in_2;  // AND_Gate and_1, 32 bits wide
  assign o_or = in_1 | in_2;  // OR_Gate or_1, 32 bits wide
  assign o_xor = in_1 ^ in_2;  // XOR_Gate xor_1, 32 bits wide
  Shifter #(.width(32)) shifter_1 (.in(in_1), .\dist (in_2[4:0]), .out(o_sll));
  Comparator #(.width(32)) comparator_1 (.a(in_1), .b(in_2), .lt(comparator_1_lt));  // open: gt, eq
  Shifter #(.shift("lr"), .width(32)) shifter_2 (.in(in_1), .\dist (in_2[4:0]), .out(o_srl));
  Multiplier #(.width(32)) multiplier_1 (.a(in_1), .b(in_2), .out(o_mul));  // open: cin, cout
  Multiplier #(.width(32)) multiplier_2 (.a(in_1), .b(in_2), .cout(o_mulh));  // open: out, cin
  Divider #(.width(32)) divider_1 (.a(in_1), .b(in_2), .out(o_div));  // open: upper, rem
  Divider #(.width(32)) divider_2 (.a(in_1), .b(in_2), .rem(o_rem));  // open: out, upper
  Comparator #(.width(32)) comparator_2 (.a(in_1), .b(in_2), .eq(out_5));  // open: gt, lt
  Bit_Extender #(.in_width(1), .out_width(32)) bit_extender_1 (.out(o_slt));  // open: in

  // Other names for the same wires on the sheet: isEqual = out_5; OP[3:0] = in_3; result[31:0] = Outputs;
  //   X[31:0] = in_1; Y[31:0] = in_2

  // Notes on the sheet:
  //   I/O
  //   Operation Selection
  //   Inputs
  //   Operations
endmodule
